# Fritzing sketch design (saved by Fritzing 0.9.3b)
breadboards: 1

parts:
  Part1 = Arduino Uno (Rev3)
  Adafruit_HUZZAH_ESP8266_Breakout1 = Adafruit HUZZAH ESP8266 Breakout [part_number=2471]
  RHT1 = Humidity and Temperature Sensor RHT03
  GLCD_128x1 = 128 x 64 Graphic LCD
  R1 = Photocell (LDR) [package=THT]
  R2 = Resistor [tolerance=±5% resistance=10k package="2010 [SMD]"]
  Part2 = Real Time Clock Module - DS1307 RTC Breakout Board
  R3 = Resistor [tolerance=±5% resistance=220 package=THT]

nets:
  N1: Part1.A0, R1.pin_1, R2.Pin_0
  N2: Part1.A4/SDA, Part2.SDA
  N3: Part1.A5/SCL, Part2.SCL
  N4: Part1.D10_PWM/SS, RHT1.Vcc
  N5: Part1.D11_PWM/MOSI, GLCD_128x1.4_D/I
  N6: Part1.D12/MISO, GLCD_128x1.5_R/W
  N7: Part1.D13/SCK, GLCD_128x1.6_Enable
  5V: Part1.5V, Adafruit_HUZZAH_ESP8266_Breakout1.A, RHT1.Data-signal, GLCD_128x1.2_Vdd, R1.pin_0, Part2.5V, R3.Pin_1
  GND: Part1.GND, Adafruit_HUZZAH_ESP8266_Breakout1.EN, RHT1.GND_1, RHT1.GND_2, R2.Pin_1, Part2.GND
  N8: Adafruit_HUZZAH_ESP8266_Breakout1.GND, Adafruit_HUZZAH_ESP8266_Breakout1.VBat, Adafruit_HUZZAH_ESP8266_Breakout1.V+, Adafruit_HUZZAH_ESP8266_Breakout1.#13, Adafruit_HUZZAH_ESP8266_Breakout1.#12, Adafruit_HUZZAH_ESP8266_Breakout1.#2, Adafruit_HUZZAH_ESP8266_Breakout1.#15, Adafruit_HUZZAH_ESP8266_Breakout1.3V, Adafruit_HUZZAH_ESP8266_Breakout1.LDO
  N9: GLCD_128x1.1_Vss, GLCD_128x1.16_CS2, GLCD_128x1.20_K(-)
  N10: GLCD_128x1.19_A(+), R3.Pin_0
